# Fritzing sketch diagram (saved by Fritzing 0.9.3b)
breadboards: 1

parts:
  Raspberry_Pi_1 = Raspberry Pi 3 [part_number=RPI-3-V1.2]
  S1 = Pushbutton [package=THT]
  S2 = Pushbutton [package=THT]
  LED1 = LED - 5mm [color="Red (633nm)" package="5 mm [THT]"]
  R1 = Resistor [tolerance=±5% resistance=220 package=THT]

nets:
  N1: Raspberry_Pi_1.GPIO2, S2.leg1
  N2: Raspberry_Pi_1.GPIO3, S1.leg1
  N3: Raspberry_Pi_1.GPIO17, R1.Pin_1
  N4: Raspberry_Pi_1.GND, S1.leg0, S2.leg0, LED1.cathode
  N5: LED1.anode, R1.Pin_0
